# Fritzing sketch Gun (saved by Fritzing 0.9.2b)
circuit board: 2.63344cm x 4.34996cm
breadboards: 1

parts:
  R1 = Resistor [tolerance=±5% resistance=220 package=THT]
  J2 = female pin header, 2 pins [form="♀ (female)"]
  J3 = female pin header, 2 pins [form="♀ (female)"]
  J1 = female pin header, 2 pins [form="♀ (female)"]
  ARDUINO = Arduino Pro Mini v13
  Q2 = NPN-Transistor [package="TO92 [THT]"]
  VCC = Battery block 9V
  U5 = Voltage Regulator LM1117 [package=sot223]
  J6 = female pin header, 7 pins [form="♀ (female)"]
  C1 = Ceramic Capacitor [capacitance=100nF package="0805 [SMD, multilayer]"]

nets:
  GND: R1.Pin_0, J2.pin2, J3.pin2, Q2.E, VCC.-, U5.IN, J6.pin5
  N1: R1.Pin_1, ARDUINO.D3_PWM, Q2.B
  N2: J2.pin1, ARDUINO.D4
  N3: J3.pin1, ARDUINO.D5_PWM
  N4: J1.pin1, ARDUINO.RAW, VCC.+
  N5: J1.pin2, Q2.C
  N6: ARDUINO.D13/SCK, J6.pin3
  N7: ARDUINO.D12/MISO, J6.pin2
  N8: ARDUINO.D11_PWM/MOSI, J6.pin1
  N9: ARDUINO.D9_PWM, J6.pin6
  N10: ARDUINO.D8, J6.pin7
  N11: U5.ADJ, C1.1
  N12: U5.OUT, J6.pin4, C1.0

// code stored in the sketch: Gun.ino

